# Fritzing sketch 3DPB-Schematic-Episode-02 (saved by Fritzing 0.9.4)

parts:
  Microcontroller = IC, DIP package, 40 pins [chip_label=ATMEGA1284P]
  R1 = Resistor [tolerance=±5% resistance=10k package=THT]
  R2 = Resistor [tolerance=±5% resistance=220 package=THT]
  Power_LED = LED - 3mm [color="Red (635nm)" package="3 mm [THT]"]
  Crystal = Crystal [frequency="16 Mhz" package=SMD]
  C1 = Ceramic Capacitor [capacitance=22pF package="100 mil [THT, multilayer]"]
  C2 = Ceramic Capacitor [capacitance=22pF package="100 mil [THT, multilayer]"]
  R3 = Resistor [tolerance=±5% resistance=220 package=THT]
  Power_LED1 = LED - 3mm [color="Green (565nm)" package="3 mm [THT]"]
  ICSP = AVR ISP 6 Pin [package=2x3-ns]
  Reset_Switch = Pushbutton [package="[SMD]"]
  C3 = Ceramic Capacitor [capacitance=10µF package="100 mil [THT, multilayer]"]

nets:
  MOSI: Microcontroller.pin6, ICSP.4
  MISO: Microcontroller.pin7, ICSP.1
  SCK: Microcontroller.pin8, R3.Pin_0, ICSP.3
  RESET: Microcontroller.pin9, R1.Pin_1, ICSP.5, Reset_Switch.Pin_3, Reset_Switch.Pin_4, C3.1
  5V: Microcontroller.pin10, Microcontroller.pin30, Microcontroller.pin32, R1.Pin_0, R2.Pin_0, ICSP.2
  GND: Microcontroller.pin11, Microcontroller.pin31, Power_LED.cathode, C1.0, C2.0, Power_LED1.cathode, ICSP.6, Reset_Switch.Pin_1, Reset_Switch.Pin_2, C3.0
  XTAL2: Microcontroller.pin12, Crystal.pin_1, C2.1
  XTAL1: Microcontroller.pin13, Crystal.pin_0, C1.1
  RX: Microcontroller.pin14
  TX: Microcontroller.pin15
  N1: R2.Pin_1, Power_LED.anode
  N2: R3.Pin_1, Power_LED1.anode

notes:
  3D Printer Board - Episode 2, Base circuit diagram for 3D printer main board., 1.0
  Power LED
  Clock
  Reset
  Comm Status LED
  Programming Header
