# Fritzing sketch 3DPB-Schematic-Episode-09 (saved by Fritzing 0.9.4)
breadboards: 1

parts:
  X_End_Stop_Switch = SWITCH-MOMENTARY-2 [package=tactile-pth]
  R1 = Resistor [tolerance=±5% resistance=10k package=THT]
  Microcontroller = IC, DIP package, 40 pins [chip_label=ATMEGA1284P]
  Y_End_Stop_Switch = SWITCH-MOMENTARY-2 [package=tactile-pth]
  R2 = Resistor [tolerance=±5% resistance=10k package=THT]
  Z_End_Stop_Switch = SWITCH-MOMENTARY-2 [package=tactile-pth]
  R3 = Resistor [tolerance=±5% resistance=10k package=THT]

nets:
  X-STOP: X_End_Stop_Switch.1, R1.Pin_1, Microcontroller.pin24
  5V: X_End_Stop_Switch.2, Microcontroller.pin10, Microcontroller.pin30, Microcontroller.pin32, Y_End_Stop_Switch.2, Z_End_Stop_Switch.2
  GND: R1.Pin_0, Microcontroller.pin11, Microcontroller.pin31, R2.Pin_0, R3.Pin_0
  Y-STOP: Microcontroller.pin25, Y_End_Stop_Switch.1, R2.Pin_1
  Z-STOP: Microcontroller.pin26, Z_End_Stop_Switch.1, R3.Pin_1

notes:
  3D Printer Board - Episode 9, End stop diagram for 3D printer main board., 1.0
  X End Stop
  Y End Stop
  Z End Stop
